# Fritzing sketch HomeControlMonitor-Simple2 (saved by Fritzing 0.9.2b)
circuit board: 6cm x 3.8cm
breadboards: 1

parts:
  USB_Power_in = USB Connectors [package=usb-a-h]  # not connected
  C1 = Electrolytic Capacitor [capacitance=0.1mF package="100 mil [THT, electrolytic]"]
  C2 = Ceramic Capacitor [capacitance=100nF package="100 mil [THT, multilayer]"]
  Adafruit_HUZZAH_ESP8266_Breakout1 = Adafruit HUZZAH ESP8266 Breakout [part_number=2471]
  J3 = 1.44-128x128-SPI-TFT-display-ILI9163 [package=THT]
  J2 = female pin header, 2 pins [form="♀ (female)"]
  J1 = female pin header, 2 pins [form="♀ (female)"]
  J4 = female pin header, 2 pins [form="♀ (female)"]

nets:
  GND: C1.-, C2.1, Adafruit_HUZZAH_ESP8266_Breakout1.GND, J3.pin2, J1.pin2
  5V: C1.+, C2.0, Adafruit_HUZZAH_ESP8266_Breakout1.VBat, J3.pin1, J1.pin1
  N1: Adafruit_HUZZAH_ESP8266_Breakout1.#13, J3.pin7
  N2: Adafruit_HUZZAH_ESP8266_Breakout1.#12, J3.pin3
  N3: Adafruit_HUZZAH_ESP8266_Breakout1.#14, J3.pin6
  N4: Adafruit_HUZZAH_ESP8266_Breakout1.#16, J3.pin5
  N5: Adafruit_HUZZAH_ESP8266_Breakout1.TX, J2.pin2
  N6: Adafruit_HUZZAH_ESP8266_Breakout1.RX, J2.pin1
  N7: Adafruit_HUZZAH_ESP8266_Breakout1.#0, J4.pin1
  N8: Adafruit_HUZZAH_ESP8266_Breakout1.#2, J4.pin2
  3.3V: Adafruit_HUZZAH_ESP8266_Breakout1.3V, J3.pin4, J3.pin8

notes:
  VCC in
  128x128 SPI TFT
  - +
  Home Controll Monitor, 1
  Vcc => 5V
  Gnd => Gnd
  CS => IO12
  RST => 3.3V
  A0 => IO16
  SDA => IO14
  SCK => IO13
  LED => 3.3V
  TX-RX
  0 2

custom parts:
  1.44-128x128-SPI-TFT-display-ILI9163: 1.44" 128x128 TFT display SPI interface Controll chip ILI9163 8 Pin interface
